# Fritzing sketch PCB_share (saved by Fritzing 0.9.2b)
circuit board: 5.78482cm x 4.92714cm
perfboards: 1

parts:
  S1 = Pushbutton [package="[THT]"]
  S3 = Pushbutton [package="[THT]"]
  S4 = Pushbutton [package="[THT]"]
  元件1 = Arduino Pro Mini v13
  RPI = female pin header, 20 pins [form="♀ (female)"]
  RPI_2 = female pin header, 20 pins [form="♀ (female)"]
  2110LCD = female pin header, 8 pins [form="♀ (female)"]
  S2 = Pushbutton [package="[THT]"]
  R1 = Resistor [tolerance=±5% resistance=10k package=THT]
  servo = female pin header, 2 pins [form="♀ (female)"]
  DC = female pin header, 2 pins [form="♀ (female)"]

nets:
  N1: S1.Pin_1, S1.Pin_2, S3.Pin_1, S3.Pin_2, S4.Pin_1, S4.Pin_2, 元件1.VCC, RPI.pin1, 2110LCD.pin6, S2.Pin_1, S2.Pin_2
  N2: S1.Pin_3, S1.Pin_4, RPI_2.pin6
  N3: S3.Pin_3, S3.Pin_4, RPI.pin6
  N4: S4.Pin_3, S4.Pin_4, RPI.pin4
  GND: 元件1.GND, RPI_2.pin3, 2110LCD.pin8, R1.Pin_1, DC.pin2
  N5: 元件1.A4, RPI.pin2
  N6: 元件1.A5, RPI.pin3
  N7: 元件1.D13/SCK, 2110LCD.pin5
  N8: 元件1.D11_PWM/MOSI, 2110LCD.pin4
  N9: 元件1.D10_PWM/SS, servo.pin1
  N10: 元件1.D9_PWM, servo.pin2
  N11: 元件1.D8, RPI.pin7
  N12: 元件1.D7, S2.Pin_3, S2.Pin_4, R1.Pin_0
  N13: 元件1.D5_PWM, 2110LCD.pin3
  N14: 元件1.D4, 2110LCD.pin2
  N15: 元件1.D3_PWM, 2110LCD.pin1
  N16: 元件1.D2, 2110LCD.pin7
  N17: RPI_2.pin1, DC.pin1
